// Logisim project labqsn.circ as structural Verilog: 3 circuits, main circuit main
module main (
  input  X3,
  input  Y2,
  input  Y1,
  input  X2,
  input  X1,
  input  X0,
  input  Y3,
  input  Y0,
  input  C0,
  output C1,
  output C2,
  output C3,
  output C4,
  output S0,
  output S1,
  output S2,
  output S3
);

  wire and_1_out, and_2_out, and_3_out, and_4_out, and_5_out, and_6_out, and_7_out, and_8_out, and_9_out,
       and_10_out, and_11_out, and_12_out, and_13_out, and_14_out, xor_1_out, xor_3_out, xor_5_out, xor_7_out;

  and and_1 (and_1_out, X0, Y0);
  xor xor_1 (xor_1_out, X0, Y0);
  xor xor_2 (S0, C0, xor_1_out);
  and and_2 (and_2_out, X1, Y1);
  xor xor_3 (xor_3_out, X1, Y1);
  xor xor_4 (S1, xor_3_out, C1);
  and and_3 (and_3_out, X2, Y2);
  xor xor_5 (xor_5_out, X2, Y2);
  xor xor_6 (S2, xor_5_out, C2);
  and and_4 (and_4_out, X3, Y3);
  xor xor_7 (xor_7_out, X3, Y3);
  xor xor_8 (S3, xor_7_out, C3);
  and and_5 (and_5_out, xor_1_out, C0);
  and and_6 (and_6_out, xor_3_out, and_1_out);
  and and_7 (and_7_out, xor_3_out, xor_1_out, C0);
  and and_8 (and_8_out, xor_5_out, and_2_out);
  and and_9 (and_9_out, xor_5_out, xor_3_out, and_1_out);
  and and_10 (and_10_out, xor_5_out, xor_3_out, xor_1_out, C0);
  and and_11 (and_11_out, xor_7_out, and_3_out);
  and and_12 (and_12_out, xor_7_out, xor_5_out, and_2_out);
  and and_13 (and_13_out, xor_7_out, xor_5_out, xor_3_out, and_1_out);
  and and_14 (and_14_out, xor_7_out, xor_5_out, xor_3_out, xor_1_out, C0);
  or or_1 (C1, and_1_out, and_5_out);
  or or_2 (C2, and_2_out, and_6_out, and_7_out);
  or or_3 (C3, and_3_out, and_8_out, and_9_out, and_10_out);
  or or_4 (C4, and_4_out, and_11_out, and_12_out, and_13_out, and_14_out);

  // Notes on the sheet:
  //   P3
endmodule

module LOOKAHEAD (
  input  [3:0] Y,
  input  [3:0] X,
  input  C0,
  output C1,
  output C2,
  output C3,
  output C4,
  output S0,
  output S1,
  output S2,
  output S3
);

  wire and_1_out, and_2_out, and_3_out, and_4_out, and_5_out, and_6_out, and_7_out, and_8_out, xor_1_out,
       xor_3_out, xor_5_out, xor_7_out;

  xor xor_1 (xor_1_out, Y[1], X[1]);
  and and_1 (and_1_out, X[1], Y[1]);
  xor xor_2 (S0, xor_1_out, C0);
  and and_2 (and_2_out, C0, xor_1_out);
  or or_1 (C1, and_2_out, and_1_out);
  xor xor_3 (xor_3_out, X[1], Y[1]);
  and and_3 (and_3_out, X[1], Y[1]);
  and and_4 (and_4_out, C1, xor_3_out);
  xor xor_4 (S1, xor_3_out, C1);
  or or_2 (C2, and_4_out, and_3_out);
  xor xor_5 (xor_5_out, X[2], Y[2]);
  and and_5 (and_5_out, X[2], Y[2]);
  and and_6 (and_6_out, C2, xor_5_out);
  xor xor_6 (S2, xor_5_out, C2);
  or or_3 (C3, and_6_out, and_5_out);
  xor xor_7 (xor_7_out, X[3], Y[3]);
  and and_7 (and_7_out, X[3], Y[3]);
  and and_8 (and_8_out, C3, xor_7_out);
  xor xor_8 (S3, xor_7_out, C3);
  or or_4 (C4, and_8_out, and_7_out);

  assign X[0] = X[1];
  assign Y[0] = Y[1];

  // Notes on the sheet:
  //   P0
  //   G0
  //   G1
  //   P1
  //   P2
  //   G2
  //   P3
  //   G3
endmodule

module LOOKAHEAD_ONE (
  input  X3,
  input  Y2,
  input  Y1,
  input  X2,
  input  X1,
  input  X0,
  input  Y3,
  input  Y0,
  input  C0,
  output C1,
  output C2,
  output C3,
  output C4,
  output S0,
  output S1,
  output S2,
  output S3
);

  wire and_1_out, and_2_out, and_3_out, and_4_out, and_5_out, and_6_out, and_7_out, and_8_out, and_9_out,
       and_10_out, and_11_out, and_12_out, and_13_out, and_14_out, xor_1_out, xor_3_out, xor_5_out, xor_7_out;

  and and_1 (and_1_out, X0, Y0);
  xor xor_1 (xor_1_out, X0, Y0);
  xor xor_2 (S0, C0, xor_1_out);
  and and_2 (and_2_out, X1, Y1);
  xor xor_3 (xor_3_out, X1, Y1);
  xor xor_4 (S1, xor_3_out, C1);
  and and_3 (and_3_out, X2, Y2);
  xor xor_5 (xor_5_out, X2, Y2);
  xor xor_6 (S2, xor_5_out, C2);
  and and_4 (and_4_out, X3, Y3);
  xor xor_7 (xor_7_out, X3, Y3);
  xor xor_8 (S3, xor_7_out, C3);
  and and_5 (and_5_out, xor_1_out, C0);
  and and_6 (and_6_out, xor_3_out, and_1_out);
  and and_7 (and_7_out, xor_3_out, xor_1_out, C0);
  and and_8 (and_8_out, xor_5_out, and_2_out);
  and and_9 (and_9_out, xor_5_out, xor_3_out, and_1_out);
  and and_10 (and_10_out, xor_5_out, xor_3_out, xor_1_out, C0);
  and and_11 (and_11_out, xor_7_out, and_3_out);
  and and_12 (and_12_out, xor_7_out, xor_5_out, and_2_out);
  and and_13 (and_13_out, xor_7_out, xor_5_out, xor_3_out, and_1_out);
  and and_14 (and_14_out, xor_7_out, xor_5_out, xor_3_out, xor_1_out, C0);
  or or_1 (C1, and_1_out, and_5_out);
  or or_2 (C2, and_2_out, and_6_out, and_7_out);
  or or_3 (C3, and_3_out, and_8_out, and_9_out, and_10_out);
  or or_4 (C4, and_4_out, and_11_out, and_12_out, and_13_out, and_14_out);

  // Notes on the sheet:
  //   P3
endmodule
